# Fritzing sketch pcb (saved by Fritzing 0.9.3b)
circuit board: 15.24cm x 15.24cm
breadboards: 1

parts:
  part = Analog Digital MUX Breakout
  part_2 = Header 5x2 [package=avr_icsp]
  part_3 = male pin header, 10 pins [form="♂ (male)"]
  part_4 = male pin header, 10 pins [form="♂ (male)"]
  part_5 = female pin header, 8 pins [form="♀ (female)"]
  part_6 = female pin header, 8 pins [form="♀ (female)"]
  part_7 = female pin header, 8 pins [form="♀ (female)"]
  part_8 = female pin header, 8 pins [form="♀ (female)"]
  part_9 = Analog Digital MUX Breakout
  part_10 = Header 5x2 [package=avr_icsp]
  part_11 = male pin header, 10 pins [form="♂ (male)"]
  part_12 = male pin header, 10 pins [form="♂ (male)"]
  part_13 = female pin header, 8 pins [form="♀ (female)"]
  part_14 = female pin header, 8 pins [form="♀ (female)"]
  part_15 = Analog Digital MUX Breakout
  part_16 = Header 5x2 [package=avr_icsp]
  part_17 = male pin header, 10 pins [form="♂ (male)"]
  part_18 = male pin header, 10 pins [form="♂ (male)"]
  part_19 = female pin header, 8 pins [form="♀ (female)"]
  part_20 = female pin header, 8 pins [form="♀ (female)"]
  part_21 = Analog Digital MUX Breakout
  part_22 = Header 5x2 [package=avr_icsp]
  part_23 = male pin header, 10 pins [form="♂ (male)"]
  part_24 = male pin header, 10 pins [form="♂ (male)"]
  part_25 = SparkFun Pro Micro
  part_26 = Header 5x2 [package=avr_icsp]

nets:
  N1: part.C0, part_5.pin3
  N2: part.C1, part_5.pin2
  N3: part.C2, part_5.pin1
  N4: part.C3, part_5.pin4
  N5: part.C4, part_5.pin5
  N6: part.C5, part_5.pin6
  N7: part.C6, part_5.pin7
  N8: part.C7, part_5.pin8
  N9: part.C8, part_6.pin8
  N10: part.C9, part_6.pin7
  N11: part.C10, part_6.pin6
  N12: part.C11, part_6.pin5
  N13: part.C12, part_6.pin4
  N14: part.C13, part_6.pin1
  N15: part.C14, part_6.pin2
  N16: part.C15, part_6.pin3
  N17: part.GND, part_2.1, part_4.pin1, part_4.pin2, part_4.pin3, part_4.pin4, part_4.pin5, part_4.pin6, part_4.pin7, part_4.pin8, part_4.pin9, part_4.pin10
  N18: part.VCC, part_2.2, part_3.pin1, part_3.pin2, part_3.pin3, part_3.pin4, part_3.pin5, part_3.pin6, part_3.pin7, part_3.pin8, part_3.pin9, part_3.pin10
  N19: part.S0, part_2.4
  N20: part.S1, part_2.6
  N21: part.S2, part_2.8
  N22: part.S3, part_2.10
  N23: part.SIG, part_2.7
  N24: part_7.pin1, part_9.C2
  N25: part_7.pin2, part_9.C1
  N26: part_7.pin3, part_9.C0
  N27: part_7.pin4, part_9.C3
  N28: part_7.pin5, part_9.C4
  N29: part_7.pin6, part_9.C5
  N30: part_7.pin7, part_9.C6
  N31: part_7.pin8, part_9.C7
  N32: part_8.pin1, part_9.C13
  N33: part_8.pin2, part_9.C14
  N34: part_8.pin3, part_9.C15
  N35: part_8.pin4, part_9.C12
  N36: part_8.pin5, part_9.C11
  N37: part_8.pin6, part_9.C10
  N38: part_8.pin7, part_9.C9
  N39: part_8.pin8, part_9.C8
  N40: part_9.GND, part_10.1, part_12.pin1, part_12.pin2, part_12.pin3, part_12.pin4, part_12.pin5, part_12.pin6, part_12.pin7, part_12.pin8, part_12.pin9, part_12.pin10
  N41: part_9.VCC, part_10.2, part_11.pin1, part_11.pin2, part_11.pin3, part_11.pin4, part_11.pin5, part_11.pin6, part_11.pin7, part_11.pin8, part_11.pin9, part_11.pin10
  N42: part_9.S0, part_10.4
  N43: part_9.S1, part_10.6
  N44: part_9.S2, part_10.8
  N45: part_9.S3, part_10.10
  N46: part_9.SIG, part_10.9
  N47: part_13.pin1, part_15.C2
  N48: part_13.pin2, part_15.C1
  N49: part_13.pin3, part_15.C0
  N50: part_13.pin4, part_15.C3
  N51: part_13.pin5, part_15.C4
  N52: part_13.pin6, part_15.C5
  N53: part_13.pin7, part_15.C6
  N54: part_13.pin8, part_15.C7
  N55: part_14.pin1, part_15.C13
  N56: part_14.pin2, part_15.C14
  N57: part_14.pin3, part_15.C15
  N58: part_14.pin4, part_15.C12
  N59: part_14.pin5, part_15.C11
  N60: part_14.pin6, part_15.C10
  N61: part_14.pin7, part_15.C9
  N62: part_14.pin8, part_15.C8
  N63: part_15.GND, part_16.1, part_18.pin1, part_18.pin2, part_18.pin3, part_18.pin4, part_18.pin5, part_18.pin6, part_18.pin7, part_18.pin8, part_18.pin9, part_18.pin10
  N64: part_15.VCC, part_16.2, part_17.pin1, part_17.pin2, part_17.pin3, part_17.pin4, part_17.pin5, part_17.pin6, part_17.pin7, part_17.pin8, part_17.pin9, part_17.pin10
  N65: part_15.S0, part_16.4
  N66: part_15.S1, part_16.6
  N67: part_15.S2, part_16.8
  N68: part_15.S3, part_16.10
  N69: part_15.SIG, part_16.5
  N70: part_19.pin1, part_21.C2
  N71: part_19.pin2, part_21.C1
  N72: part_19.pin3, part_21.C0
  N73: part_19.pin4, part_21.C3
  N74: part_19.pin5, part_21.C4
  N75: part_19.pin6, part_21.C5
  N76: part_19.pin7, part_21.C6
  N77: part_19.pin8, part_21.C7
  N78: part_20.pin1, part_21.C13
  N79: part_20.pin2, part_21.C14
  N80: part_20.pin3, part_21.C15
  N81: part_20.pin4, part_21.C12
  N82: part_20.pin5, part_21.C11
  N83: part_20.pin6, part_21.C10
  N84: part_20.pin7, part_21.C9
  N85: part_20.pin8, part_21.C8
  N86: part_21.GND, part_22.1, part_24.pin1, part_24.pin2, part_24.pin3, part_24.pin4, part_24.pin5, part_24.pin6, part_24.pin7, part_24.pin8, part_24.pin9, part_24.pin10
  N87: part_21.VCC, part_22.2, part_23.pin1, part_23.pin2, part_23.pin3, part_23.pin4, part_23.pin5, part_23.pin6, part_23.pin7, part_23.pin8, part_23.pin9, part_23.pin10
  N88: part_21.S0, part_22.4
  N89: part_21.S1, part_22.6
  N90: part_21.S2, part_22.8
  N91: part_21.S3, part_22.10
  N92: part_21.SIG, part_22.3
  N93: part_25.GND, part_26.1
  N94: part_25.10, part_26.10
  N95: part_25.16, part_26.8
  N96: part_25.14, part_26.6
  N97: part_25.15, part_26.4
  N98: part_25.A0, part_26.9
  N99: part_25.A1, part_26.7
  N100: part_25.A2, part_26.5
  N101: part_25.A3, part_26.3
  N102: part_25.VCC, part_26.2

custom parts:
  SparkFun Pro Micro: The Pro Micro is similar to the Pro Mini except with an ATmega32U4 on board. The USB transceiver inside the 32U4 allows us to add USB connectivity on-board and do away with bulky external USB interface. Based on: https://github.com/unorthodox-engineers/unorthodox-arduino/blob/master/Unorthodox/fritzing/parts/Pro%20Micro.fzpz
